# Fritzing sketch ESP8266-01-TO-FTDI- (saved by Fritzing 0.9.3b)
breadboards: 1

parts:
  Part1 = FTDI Basic Programmer
  U1 = ESP8266 WiFi Module [part_number=ESP8266]
  PSU1 = Adjustable Breadboard Power Supply

nets:
  N1: Part1.RXI, U1.TXD
  N2: Part1.TXO, U1.RXD
  GND: Part1.GND, U1.GPIO_0, U1.CH_PD, U1.GND, PSU1.Vout-
  N3: U1.VCC, PSU1.Vout+

custom parts:
  ESP8266 WiFi Module: Generic WiFi Module based on the ESP8266 with onboard PCB antenna and UART communications
